# Fritzing sketch power (saved by Fritzing 0.9.6b)
circuit board: 2.29534cm x 4.5cm
breadboards: 1

parts:
  BAT1 = Battery Holders [package=lipo-1100mAh]
  TP1 = TP4056 [chip_label=TP4056 package="DIP (Dual Inline) [THT]"]
  U2 = Voltage Regulator - 3.3V [part_number=MCP1700 package="TO220 [THT]"]
  JP11 = Header 2 [package=jst-2-pth-ns]
  C1 = Capacitor Polarized [package=cpol-radial-100uf-25v]
  JP2_[JP1_IN] = Header 2 [package=jst-2-pth-ns]
  JP1_[OUT] = Header 2 [package=jst-2-pth-ns]
  JP4_[JP3_IN] = Header 2 [package=jst-2-pth-ns]
  JP3_[OUT] = Header 2 [package=jst-2-pth-ns]
  JP5_[OUT] = Header 2 [package=jst-2-pth-ns]
  JP6 = Header 2 [package=jst-2-pth-ns]
  JP8_[IN/OUT] = Header 2 [package=jst-2-pth-ns]
  JP7 = Header 2 [package=jst-2-pth-ns]
  JP9 = Header 2 [package=jst-2-pth-ns]
  JP10_[JP9_IN] = Header 2 [package=jst-2-pth-ns]
  D4 = Rectifier Diode [package="Melf DO-213 AA [SMD]"]
  D5 = Rectifier Diode [package="Melf DO-213 AA [SMD]"]
  D6 = Rectifier Diode [package="Melf DO-213 AA [SMD]"]
  U3 = SWITCH_SPDT [package=kps-1290]
  D1 = SOLAR-IXYS [package=solarbit-12x1]
  D2 = SOLAR-IXYS [package=solarbit-12x1]
  D3 = SOLAR-IXYS [package=solarbit-12x1]
  C2 = Ceramic Capacitor [capacitance="100 nF" voltage=35V package="100 mil [THT, multilayer]"]

nets:
  N1: BAT1.+, JP8_[IN/OUT].2
  N2: BAT1.-, JP8_[IN/OUT].1
  N3: TP1.pin1, JP4_[JP3_IN].2
  N4: TP1.pin2, JP4_[JP3_IN].1
  N5: TP1.pin3, JP5_[OUT].2
  N6: TP1.pin6, JP5_[OUT].1
  N7: U2.input_voltage, JP11.2, C1.+, JP6.1, JP7.1, JP9.1, C2.1
  N8: U2.GND, JP11.1, C1.-, JP6.2, JP7.2, C2.0
  N9: U2.output_voltage, JP9.2
  N10: JP2_[JP1_IN].1, JP3_[OUT].1
  N11: JP2_[JP1_IN].2, JP3_[OUT].2
  N12: JP1_[OUT].1, D1.A, D2.A, D3.A
  N13: JP1_[OUT].2, D4.cathode, D5.cathode, D6.cathode
  N14: JP10_[JP9_IN].1, U3.O
  N15: JP10_[JP9_IN].2, U3.P
  N16: D4.anode, D2.C
  N17: D5.anode, D1.C
  N18: D6.anode, D3.C

custom parts:
  TP4056: A DIP stand-in part for whatever IC you want. With 6 pins on a 300mil dual inline package (DIP) footprint.
